# Fritzing sketch AutoSwitch (saved by Fritzing 0.9.3b)

parts:
  Composant1 = Arduino Nano (Rev3.0)
  ACS712_Current_Sensor1 = ACS712 Current Sensor
  2_Channel_Relay1 = 2 Channel Power Relay
  J1 = Camdenboss CTB0158-3 [part_number=CTB0158-3 package=THT]
  J2 = Camdenboss CTB0158-3 [part_number=CTB0158-3 package=THT]
  J3 = Camdenboss CTB0158-3 [part_number=CTB0158-3 package=THT]
  Power_plug1 = Power plug

nets:
  N1: Composant1.D2, 2_Channel_Relay1.IN2
  VIN: Composant1.VIN, Power_plug1.VCC
  GND: Composant1.GND, ACS712_Current_Sensor1.GND, Power_plug1.GND
  5V: Composant1.5V, ACS712_Current_Sensor1.VCC
  N2: Composant1.A2, ACS712_Current_Sensor1.OUT
  N3: 2_Channel_Relay1.K2-COM, J1.pin1
  N4: 2_Channel_Relay1.K2-NO, J3.pin3
  N5: J1.pin2, J2.pin2
  N6: J1.pin3, J2.pin1

notes:
  5V power supply
  AC POWER
  TOOL
  VACUUM
  AUTOSWITCH

custom parts:
  ACS712 Current Sensor: A breakout board for the Allegro ACS712 is a Hall Effect-based linear current sensor. The module operates at 5V.
  2 Channel Power Relay: A 2 channel power relay. The module operates at 5V.
